# Fritzing sketch Node 3 (saved by Fritzing 0.9.3b)

parts:
  U1 = ESP 32 DEVKIT DOIT
  DHT1 = DHT11 Humitidy and Temperature Sensor
  Part1 = MQ-3 breakout

nets:
  N1: U1.D22, U1.D4, DHT1.NULL
  N2: U1.VP, Part1.AO

custom parts:
  DHT11 Humitidy and Temperature Sensor: DHT11 Humidity and Temperature Sensor
  MQ-3 breakout: Alcohol sensor is capable of detecting alcohol (ethanol) particles on itself and gives the information in digital form back to us to manipulate with it. SKU:101251 • Voltage: 5V DC • Power: max 750mW • Measurement range: 0.04-4mg/L
